# Fritzing sketch HMS (saved by Fritzing 0.9.9b)

parts:
  LCD2004-I2C1 = LCD2004-I2C
  Part1 = Arduino Nano (Rev3.0)
  ZS-042_RTC1 = ZS-042 RTC Module
  Part3 = BME280
  TD-er1 = MH-Z19 CO2 sensor [part_number=MH-Z19]
  S1 = Pushbutton [package="[SMD]"]

nets:
  GND: LCD2004-I2C1.GND, Part1.GND, ZS-042_RTC1.GND, Part3.GND, TD-er1.GND, S1.Pin_1, S1.Pin_2
  VCC: LCD2004-I2C1.VCC, Part1.5V, ZS-042_RTC1.VCC, Part3.VIN, TD-er1.Vin
  N1: LCD2004-I2C1.SDA, Part1.A4, ZS-042_RTC1.SDA, Part3.SDA
  N2: LCD2004-I2C1.SCL, Part1.A5, ZS-042_RTC1.SCL, Part3.SCL
  N3: Part1.D2, TD-er1.TX
  N4: Part1.D3, TD-er1.RX
  N5: TD-er1.HD, S1.Pin_3

custom parts:
  LCD2004-I2C: A standard character display with 4x20 characters. Comes in many colors with LCM2004 IIC attached.
